# Fritzing sketch temperature_reader_esp32_blynk_schematics (saved by Fritzing 0.9.6b)
breadboards: 1

parts:
  RHT1 = Humidity and Temperature Sensor RHT03
  Mod1 = Heltec WiFi LoRa 32 V2 [part_number=HTIT-WB32LA]

nets:
  N1: RHT1.Vcc, Mod1.pin_20
  N2: RHT1.Data-signal, Mod1.pin_34
  N3: RHT1.GND_1, Mod1.GND
  N4: Mod1.pin_16, Mod1.pin_17
  N5: Mod1.pin_21, Mod1.pin_22
